// Logisim project FullAdder.circ as structural Verilog: 1 circuit, main circuit main
module main (
  input  A,
  input  B,
  input  C,
  output Sum,
  output Carry
);

  wire and_1_out, and_2_out, and_3_out;

  ExactlyOne xor_1 (.out(Sum), .in0(A), .in1(B), .in2(C));
  and and_1 (and_1_out, A, C);
  and and_2 (and_2_out, A, B);
  and and_3 (and_3_out, B, C);
  or or_1 (Carry, and_1_out, and_2_out, and_3_out);
endmodule
