// Logisim project FullSubtractore.circ as structural Verilog: 1 circuit, main circuit main
module main (
  input  A,
  input  B,
  input  Bin,
  output Difference,
  output Borrow
);

  wire and_1_out, and_2_out, not_1_out, not_2_out, xor_1_out;

  not not_1 (not_1_out, A);
  xor xor_1 (xor_1_out, A, B);
  not not_2 (not_2_out, xor_1_out);
  and and_1 (and_1_out, not_1_out, B);
  and and_2 (and_2_out, Bin, not_2_out);
  xor xor_2 (Difference, xor_1_out, Bin);
  or or_1 (Borrow, and_2_out, and_1_out);
endmodule
