// Logisim project Multiplexer.circ as structural Verilog: 1 circuit, main circuit main
module main (
  input  I0,
  input  I1,
  input  I2,
  input  I3,
  input  I4,
  input  I5,
  input  I6,
  input  in_8,
  input  I7,
  input  [2:0] in_10
);

  wire multiplexer_1_out, undriven;

  Multiplexer #(.select(3)) multiplexer_1 (
    .in0(I0), .in1(I1), .in2(I2), .in3(I3), .in4(I4), .in5(I5), .in6(I6), .in7(I7), .out(multiplexer_1_out),
    .sel(in_10), .en(undriven));
  LED led_1 (.in(multiplexer_1_out));
endmodule
